# Fritzing sketch zorkduino_Mini_PRO (saved by Fritzing 0.8.7b)
breadboards: 1

parts:
  Part1 = Arduino Pro Mini v13
  R5 = Resistor [tolerance=±5% resistance=1k package=THT]
  R1 = Resistor [tolerance=±5% resistance=470 package=THT]
  R6 = Resistor [tolerance=±5% resistance=100k package=THT]
  U3 = Mystery Part - 6 pins [chip_label="MicroSD Module" package=THT]
  U4 = Mystery Part - 3 pins [part_number=TSOP1822 chip_label=IR package=THT]

nets:
  N1: Part1.D0/TX, R1.Pin_0
  VCC: Part1.VCC, U3.VCC, U4.VCC
  GND: Part1.GND, U3.GND, U4.GND
  N2: Part1.D13/SCK, U3.SCK
  N3: Part1.D12/MISO, U3.MISO
  N4: Part1.D11_PWM/MOSI, U3.MOSI
  N5: Part1.D10_PWM/SS, U3.CS
  N6: Part1.D9_PWM, R5.Pin_0
  N7: Part1.D8, U4.OUT
  N8: Part1.D6_PWM, R6.Pin_0
  N9: R5.Pin_1, R1.Pin_1

notes:
  Video
  Gnd
  Audio
  *PS2 Data
  *PS2 Clock
  Zorkduino
  Pro Mini

custom parts:
  Mystery Part - 6 pins: A dummy, proxy, ersatz, stand-in part for whatever you want. With 6 pins on a 100 mil inline pin header footprint.
  Mystery Part - 3 pins: A dummy, proxy, ersatz, stand-in part for whatever you want. With 3 pins on a 100 mil inline pin header footprint.
