# Fritzing sketch zorkduino_Uno (saved by Fritzing 0.8.7b)
breadboards: 1

parts:
  Part1 = Arduino Uno (Rev3) - ICSP
  U4 = Mystery Part - 6 pins [chip_label=MicroSD package=THT]
  U5 = Mystery Part - 3 pins [part_number=TSOP4838 chip_label=IR package=THT]
  R7 = Resistor [tolerance=±5% resistance=100k package=THT]
  R8 = Resistor [tolerance=±5% resistance=470 package=THT]
  R6 = Resistor [tolerance=±5% resistance=1k package=THT]

nets:
  N1: Part1.D8, U5.OUT
  N2: Part1.D9_PWM, R6.Pin_0
  N3: Part1.D10_PWM/SS, U4.CS
  N4: Part1.D11_PWM/MOSI, U4.MOSI
  N5: Part1.D12/MISO, U4.MISO
  N6: Part1.D13/SCK, U4.SCK
  GND: Part1.GND, U4.GND, U5.GND
  N7: Part1.D1/TX, R8.Pin_0
  N8: Part1.D6_PWM, R7.Pin_0
  VCC: Part1.5V, U4.VCC, U5.VCC
  N9: R8.Pin_1, R6.Pin_1

notes:
  Audio
  Gnd
  Video
  *PS2 Clock
  *PS2 Data
  Zorkduino
  UNO

custom parts:
  Mystery Part - 6 pins: A dummy, proxy, ersatz, stand-in part for whatever you want. With 6 pins on a 100 mil inline pin header footprint.
  Mystery Part - 3 pins: A dummy, proxy, ersatz, stand-in part for whatever you want. With 3 pins on a 100 mil inline pin header footprint.
